# Fritzing sketch bbb_sequencer (saved by Fritzing 0.9.3b)
circuit board: 16.5cm x 6.7cm
breadboards: 1

parts:
  VR1 = Trimmer Potentiometer 2016 [package=THT]
  VR2 = Trimmer Potentiometer 2016 [package=THT]
  VR3 = Trimmer Potentiometer 2016 [package=THT]
  VR4 = Trimmer Potentiometer 2016 [package=THT]
  VR5 = Trimmer Potentiometer 2016 [package=THT]
  VR6 = Trimmer Potentiometer 2016 [package=THT]
  VR7 = Trimmer Potentiometer 2016 [package=THT]
  VR8 = Trimmer Potentiometer 2016 [package=THT]
  VR9 = Trimmer Potentiometer 2016 [package=THT]
  S1 = Pushbutton [package="[THT]"]
  C1 = Ceramic Capacitor [capacitance=100nF package="100 mil [THT, multilayer]"]
  S2 = Pushbutton [package="[THT]"]
  C2 = Ceramic Capacitor [capacitance=100nF package="100 mil [THT, multilayer]"]
  S3 = Pushbutton [package="[THT]"]
  C3 = Ceramic Capacitor [capacitance=100nF package="100 mil [THT, multilayer]"]
  S4 = Pushbutton [package="[THT]"]
  C4 = Ceramic Capacitor [capacitance=100nF package="100 mil [THT, multilayer]"]
  S5 = Pushbutton [package="[THT]"]
  C5 = Ceramic Capacitor [capacitance=100nF package="100 mil [THT, multilayer]"]
  S6 = Pushbutton [package="[THT]"]
  C6 = Ceramic Capacitor [capacitance=100nF package="100 mil [THT, multilayer]"]
  S7 = Pushbutton [package="[THT]"]
  C7 = Ceramic Capacitor [capacitance=100nF package="100 mil [THT, multilayer]"]
  S8 = Pushbutton [package="[THT]"]
  C8 = Ceramic Capacitor [capacitance=100nF package="100 mil [THT, multilayer]"]
  Part1 = Arduino Nano (Rev3.0)
  VR10 = Trimmer Potentiometer 2016 [package=THT]
  VR11 = Trimmer Potentiometer 2016 [package=THT]
  VR12 = Trimmer Potentiometer 2016 [package=THT]
  VR13 = Trimmer Potentiometer 2016 [package=THT]
  VR14 = Trimmer Potentiometer 2016 [package=THT]
  VR15 = Trimmer Potentiometer 2016 [package=THT]
  VR16 = Trimmer Potentiometer 2016 [package=THT]
  S9 = Pushbutton [package="[THT]"]
  S10 = Pushbutton [package="[THT]"]
  S11 = Pushbutton [package="[THT]"]
  S12 = Pushbutton [package="[THT]"]
  S13 = Pushbutton [package="[THT]"]
  S14 = Pushbutton [package="[THT]"]
  S15 = Pushbutton [package="[THT]"]
  S16 = Pushbutton [package="[THT]"]
  C9 = Ceramic Capacitor [capacitance=100nF package="100 mil [THT, multilayer]"]
  C10 = Ceramic Capacitor [capacitance=100nF package="100 mil [THT, multilayer]"]
  C11 = Ceramic Capacitor [capacitance=100nF package="100 mil [THT, multilayer]"]
  C12 = Ceramic Capacitor [capacitance=100nF package="100 mil [THT, multilayer]"]
  C13 = Ceramic Capacitor [capacitance=100nF package="100 mil [THT, multilayer]"]
  C14 = Ceramic Capacitor [capacitance=100nF package="100 mil [THT, multilayer]"]
  C15 = Ceramic Capacitor [capacitance=100nF package="100 mil [THT, multilayer]"]
  C16 = Ceramic Capacitor [capacitance=100nF package="100 mil [THT, multilayer]"]
  C17 = Ceramic Capacitor [capacitance=100nF package="100 mil [THT, multilayer]"]
  C18 = Ceramic Capacitor [capacitance=100nF package="100 mil [THT, multilayer]"]
  C19 = Ceramic Capacitor [capacitance=100nF package="100 mil [THT, multilayer]"]
  S17 = Toggle Switch [package=THT]
  LED17 = LED - 3mm [color="Red (633nm)" package="3 mm [THT]"]
  S18 = Toggle Switch [package=THT]
  VR17 = Trimmer Potentiometer 2016 [package=THT]
  C21 = Electrolytic Capacitor [capacitance=100µF package="100 mil [THT, electrolytic]"]
  C22 = Ceramic Capacitor [capacitance=100nF package="100 mil [THT, multilayer]"]
  S19 = Pushbutton [package="[THT]"]
  C23 = Ceramic Capacitor [capacitance=100nF package="100 mil [THT, multilayer]"]
  C24 = Ceramic Capacitor [capacitance=100nF package="100 mil [THT, multilayer]"]
  LED1 = LED - 5mm [color="Red (633nm)" package="5 mm [THT]"]
  LED2 = LED - 5mm [color="Red (633nm)" package="5 mm [THT]"]
  LED3 = LED - 5mm [color="Red (633nm)" package="5 mm [THT]"]
  LED4 = LED - 5mm [color="Red (633nm)" package="5 mm [THT]"]
  LED5 = LED - 5mm [color="Red (633nm)" package="5 mm [THT]"]
  LED7 = LED - 5mm [color="Red (633nm)" package="5 mm [THT]"]
  LED6 = LED - 5mm [color="Red (633nm)" package="5 mm [THT]"]
  LED8 = LED - 5mm [color="Red (633nm)" package="5 mm [THT]"]
  LED9 = LED - 5mm [color="Red (633nm)" package="5 mm [THT]"]
  LED15 = LED - 5mm [color="Red (633nm)" package="5 mm [THT]"]
  LED16 = LED - 5mm [color="Red (633nm)" package="5 mm [THT]"]
  LED13 = LED - 5mm [color="Red (633nm)" package="5 mm [THT]"]
  LED12 = LED - 5mm [color="Red (633nm)" package="5 mm [THT]"]
  LED11 = LED - 5mm [color="Red (633nm)" package="5 mm [THT]"]
  LED14 = LED - 5mm [color="Red (633nm)" package="5 mm [THT]"]
  LED10 = LED - 5mm [color="Red (633nm)" package="5 mm [THT]"]
  C25 = Ceramic Capacitor [capacitance=100nF package="100 mil [THT, multilayer]"]
  OP1 = Dual Op-Amp [package=so08]
  R40 = Resistor [tolerance=±5% resistance=1k package=THT]
  R6 = Resistor [tolerance=±5% resistance=10k package=THT]
  R7 = Resistor [tolerance=±5% resistance=10k package=THT]
  R11 = Resistor [tolerance=±5% resistance=10k package=THT]
  R10 = Resistor [tolerance=±5% resistance=10k package=THT]
  R8 = Resistor [tolerance=±5% resistance=10k package=THT]
  R9 = Resistor [tolerance=±5% resistance=10k package=THT]
  R1 = Resistor [tolerance=±5% resistance=10k package=THT]
  R16 = Resistor [tolerance=±5% resistance=10k package=THT]
  R2 = Resistor [tolerance=±5% resistance=10k package=THT]
  R15 = Resistor [tolerance=±5% resistance=10k package=THT]
  R3 = Resistor [tolerance=±5% resistance=10k package=THT]
  R14 = Resistor [tolerance=±5% resistance=10k package=THT]
  R4 = Resistor [tolerance=±5% resistance=10k package=THT]
  R13 = Resistor [tolerance=±5% resistance=10k package=THT]
  R5 = Resistor [tolerance=±5% resistance=10k package=THT]
  R12 = Resistor [tolerance=±5% resistance=10k package=THT]
  R38 = Resistor [tolerance=±5% resistance=1k package=THT]
  R39 = Resistor [tolerance=±5% resistance=1k package=THT]
  R41 = Resistor [tolerance=±5% resistance=1k package=THT]
  R42 = Resistor [tolerance=±5% resistance=1k package=THT]
  R43 = Resistor [tolerance=±5% resistance=1k package=THT]
  R44 = Resistor [tolerance=±5% resistance=1k package=THT]
  R45 = Resistor [tolerance=±5% resistance=1k package=THT]
  R46 = Resistor [tolerance=±5% resistance=1k package=THT]
  R47 = Resistor [tolerance=±5% resistance=1k package=THT]
  R48 = Resistor [tolerance=±5% resistance=1k package=THT]
  R49 = Resistor [tolerance=±5% resistance=1k package=THT]
  R50 = Resistor [tolerance=±5% resistance=1k package=THT]
  R51 = Resistor [tolerance=±5% resistance=1k package=THT]
  R52 = Resistor [tolerance=±5% resistance=1k package=THT]
  R53 = Resistor [tolerance=±5% resistance=1k package=THT]
  R34 = Resistor [tolerance=±5% resistance=1k package=THT]
  R33 = Resistor [tolerance=±5% resistance=1k package=THT]
  R37 = Resistor [tolerance=±5% resistance=10k package=THT]
  U9 = 74HC595 SMD [package="SO16 [SMD]"]
  U8 = 74HC595 SMD [package="SO16 [SMD]"]
  U6 = 74HC4067 [package=ssop24]
  U7 = 74HC4067 [package=ssop24]
  VR18 = Trimmer Potentiometer 2016 [package=THT]
  J2 = AUDIO-JACK2 [package=audio-jack]
  J4 = AUDIO-JACK2 [package=audio-jack]
  J1 = Power Jack [package=power_jack_pth]

nets:
  GND: VR1.leg1, VR2.leg1, VR3.leg1, VR4.leg1, VR5.leg1, VR6.leg1, VR7.leg1, VR8.leg1, VR9.leg1, C1.0, C2.0, C3.0, C4.0, C5.0, C6.0, C7.0, C8.0, Part1.GND, VR10.leg1, VR11.leg1, VR12.leg1, VR13.leg1, VR14.leg1, VR15.leg1, VR16.leg1, C9.0, C10.0, C11.0, C12.0, C13.0, C14.0, C15.0, C16.0, C17.0, C18.0, C19.0, LED17.cathode, S18.L2, VR17.leg1, C21.-, C22.0, C23.0, C24.0, LED1.cathode, LED2.cathode, LED3.cathode, LED4.cathode, LED5.cathode, LED7.cathode, LED6.cathode, LED8.cathode, LED9.cathode, LED15.cathode, LED16.cathode, LED13.cathode, LED12.cathode, LED11.cathode, LED14.cathode, LED10.cathode, C25.0, OP1.A_V-, R6.Pin_0, R7.Pin_0, R11.Pin_0, R10.Pin_0, R8.Pin_0, R9.Pin_0, R1.Pin_0, R16.Pin_0, R2.Pin_0, R15.Pin_0, R3.Pin_0, R14.Pin_0, R4.Pin_0, R13.Pin_0, R5.Pin_0, R12.Pin_0, R37.Pin_0, U9.GND, U9.OE, U8.GND, U8.OE, U6.GND, U6.EN, U7.GND, U7.EN, J2.SLEEVE, J4.SLEEVE, J1.GND, J1.GNDBREAK
  knob1: VR1.wiper, U7.CHAN0
  5V: VR1.leg2, VR2.leg2, VR3.leg2, VR4.leg2, VR5.leg2, VR6.leg2, VR7.leg2, VR8.leg2, VR9.leg2, S1.Pin_1, S1.Pin_2, S2.Pin_1, S2.Pin_2, S3.Pin_1, S3.Pin_2, S4.Pin_1, S4.Pin_2, S5.Pin_1, S5.Pin_2, S6.Pin_1, S6.Pin_2, S7.Pin_1, S7.Pin_2, S8.Pin_1, S8.Pin_2, Part1.5V, VR10.leg2, VR11.leg2, VR12.leg2, VR13.leg2, VR14.leg2, VR15.leg2, VR16.leg2, S9.Pin_1, S9.Pin_2, S10.Pin_1, S10.Pin_2, S11.Pin_1, S11.Pin_2, S12.Pin_1, S12.Pin_2, S13.Pin_1, S13.Pin_2, S14.Pin_1, S14.Pin_2, S15.Pin_1, S15.Pin_2, S16.Pin_1, S16.Pin_2, C17.1, C18.1, C19.1, S17.L1, VR17.leg2, C21.+, S19.Pin_1, S19.Pin_2, C24.1, C25.1, OP1.A_V+, R34.Pin_1, R33.Pin_1, U9.MR, U9.VCC, U8.MR, U8.VCC, U6.VCC, U7.VCC
  knob2: VR2.wiper, U7.CHAN1
  knob3: VR3.wiper, U7.CHAN2
  knob4: VR4.wiper, U7.CHAN3
  knob5: VR5.wiper, U7.CHAN4
  knob6: VR6.wiper, U7.CHAN5
  knob7: VR7.wiper, U7.CHAN6
  knob8: VR8.wiper, U7.CHAN7
  knob9: VR9.wiper, U7.CHAN8
  step1: S1.Pin_3, S1.Pin_4, C1.1, R1.Pin_1, U6.CHAN0
  step2: S2.Pin_3, S2.Pin_4, C2.1, R2.Pin_1, U6.CHAN1
  step3: S3.Pin_3, S3.Pin_4, C3.1, R3.Pin_1, U6.CHAN2
  step4: S4.Pin_3, S4.Pin_4, C4.1, R4.Pin_1, U6.CHAN3
  step5: S5.Pin_3, S5.Pin_4, C5.1, R5.Pin_1, U6.CHAN4
  step6: S6.Pin_3, S6.Pin_4, C6.1, R6.Pin_1, U6.CHAN5
  step7: S7.Pin_3, S7.Pin_4, C7.1, R7.Pin_1, U6.CHAN6
  step8: S8.Pin_3, S8.Pin_4, C8.1, R8.Pin_1, U6.CHAN7
  sync_input: Part1.D2, J2.TIP
  led_latch: Part1.D3, U9.ST_CP, U8.ST_CP
  addr_3: Part1.D4, U6.S3, U7.S3
  addr_2: Part1.D5, U6.S2, U7.S2
  addr_1: Part1.D6, U6.S1, U7.S1
  addr_0: Part1.D7, U6.S0, U7.S0
  sw_scan: Part1.D8, U6.COM
  sync_sw: Part1.D9, S18.COM
  led_data: Part1.D10, U8.DS
  cv_out: Part1.D11/MOSI, VR18.leg2
  led_clock: Part1.D12/MISO, U9.SH_CP, U8.SH_CP
  internal_bpm: Part1.A1, VR17.wiper
  knob_scan: Part1.A0, U7.COM
  mode: Part1.D13/SCK, S19.Pin_3, S19.Pin_4, C23.1, R37.Pin_1
  knob10: VR10.wiper, U7.CHAN9
  knob11: VR11.wiper, U7.CHAN10
  knob12: VR12.wiper, U7.CHAN11
  knob13: VR13.wiper, U7.CHAN12
  knob14: VR14.wiper, U7.CHAN13
  knob15: VR15.wiper, U7.CHAN14
  knob16: VR16.wiper, U7.CHAN15
  step9: S9.Pin_3, S9.Pin_4, C9.1, R9.Pin_1, U6.CHAN8
  step10: S10.Pin_3, S10.Pin_4, C10.1, R10.Pin_1, U6.CHAN9
  step11: S11.Pin_3, S11.Pin_4, C11.1, R11.Pin_1, U6.CHAN10
  step12: S12.Pin_3, S12.Pin_4, C12.1, R12.Pin_1, U6.CHAN11
  step13: S13.Pin_3, S13.Pin_4, C13.1, R13.Pin_1, U6.CHAN12
  step14: S14.Pin_3, S14.Pin_4, C14.1, R14.Pin_1, U6.CHAN13
  step15: S15.Pin_3, S15.Pin_4, C15.1, R15.Pin_1, U6.CHAN14
  step16: S16.Pin_3, S16.Pin_4, C16.1, R16.Pin_1, U6.CHAN15
  N1: S17.COM, J1.PWR
  N2: LED17.anode, R33.Pin_0
  N3: S18.L1, R34.Pin_0
  N4: C22.1, VR18.wiper
  N5: LED1.anode, R38.Pin_0
  N6: LED2.anode, R39.Pin_0
  N7: LED3.anode, R40.Pin_0
  N8: LED4.anode, R41.Pin_0
  N9: LED5.anode, R42.Pin_0
  N10: LED7.anode, R44.Pin_0
  N11: LED6.anode, R43.Pin_0
  N12: LED8.anode, R45.Pin_0
  N13: LED9.anode, R46.Pin_0
  N14: LED15.anode, R52.Pin_0
  N15: LED16.anode, R53.Pin_0
  N16: LED13.anode, R50.Pin_0
  N17: LED12.anode, R49.Pin_0
  N18: LED11.anode, R48.Pin_0
  N19: LED14.anode, R51.Pin_0
  N20: LED10.anode, R47.Pin_0
  N21: OP1.A_OUT, OP1.A_-IN, J4.TIP
  N22: OP1.A_+IN, VR18.leg1
  led3: R40.Pin_1, U8.Q2
  led1: R38.Pin_1, U8.Q0
  led2: R39.Pin_1, U8.Q1
  led4: R41.Pin_1, U8.Q3
  led5: R42.Pin_1, U8.Q4
  led6: R43.Pin_1, U8.Q5
  led7: R44.Pin_1, U8.Q6
  led8: R45.Pin_1, U8.Q7
  led9: R46.Pin_1, U9.Q0
  led10: R47.Pin_1, U9.Q1
  led11: R48.Pin_1, U9.Q2
  led12: R49.Pin_1, U9.Q3
  led13: R50.Pin_1, U9.Q4
  led14: R51.Pin_1, U9.Q5
  led15: R52.Pin_1, U9.Q6
  led16: R53.Pin_1, U9.Q7
  next: U9.DS, U8.Q7'

notes:
  power led
  Sync sw
  DC 5V
  Sync In
  Internal BPM
  ALL VR below=10k
  VR 10k
  VR 2k
  CV out
  unused
  Generic Input SW
  Breadboard Band, Live Sequencer, 0.1
  Arduino NANO
  Power
  74HC4067
  74HC595
  5V
  GND
  breadboard electronic musical instruments module
  Sync in
  mode
  led_clock
  cv_out
  led_data
  sync_sw
  sw_scan
  addr_0
  addr_1
  addr_2
  addr_3
  led_latch
  sync_input
  knob_scan
  internal_bpm
  Mode Switch
  +
  5V in
  Sync Switch
  Sync
  ON
  OFF
  led 1-8
  switch 1-8
  knob 1-8
  switch 9-16
  knob 9-16
  16 step
  led 9-16

custom parts:
  Trimmer Potentiometer 2016: GF063P1KB203 tokyo cosmos 6mm trimmer potentiometer. ver.2 2016
  Trimmer Potentiometer 2016: GF063P1KB203 tokyo cosmos 6mm trimmer potentiometer. ver.2 2016
